// Logisim project proyecto 2014.circ as structural Verilog: 14 circuits, main circuit Discriminate
module main (
  input  [4:0] in_1,
  input  in_2,
  input  in_3,
  input  in_4,
  output [3:0] out_5,
  output out_6,
  output out_7,
  output [1:0] out_8,
  output out_9,
  output out_10,
  output [1:0] out_11,
  output out_12,
  output out_13,
  output [2:0] out_14,
  output out_15,
  output out_16,
  output out_17,
  output out_18,
  output out_19,
  output out_20
);

  wire [2:0] circuito_combinacional_1_state_2, memoria_estados_1_out_3;

  Memoria_Estados memoria_estados_1 (
    .in_1(circuito_combinacional_1_state_2), .CLK(in_4), .out_3(memoria_estados_1_out_3));
  Circuito_combinacional circuito_combinacional_1 (
    .in_2(in_1), .WAIT(in_2), .BR(in_3), .State(memoria_estados_1_out_3), .OP_ALU(out_5), .wr_ar(out_6),
    .sel_reg(out_7), .OP_Y__SEL(out_8), .rd_dest(out_9), .en_a(out_10), .OP_ABI(out_11), .sel_d(out_12),
    .wr_sr(out_13), .OP_DBI(out_14), .wr_ir(out_15), .en_d(out_16), .rd(out_17), .wr(out_18), .wr_pc(out_19),
    .State_2(circuito_combinacional_1_state_2), .wr_Rd(out_20));

  // Notes on the sheet:
  //   Diseño standard de circuito secuencial.
endmodule

module Discriminate (
  input  [4:0] in_1,
  output [1:0] out_2
);

  wire comparator_1_lt, not_1_out;

  not not_1 (not_1_out, in_1[0]);
  Comparator #(.width(5), .mode("unsigned")) comparator_1 (
    .a(in_1), .b(5'b10011), .lt(comparator_1_lt));  // open: gt, eq
  and and_1 (out_2[1], in_1[0], in_1[1]);
  and and_2 (out_2[0], not_1_out, comparator_1_lt);

  // Notes on the sheet:
  //   ALU = 01
  //   DBI = 10
  //   COND = 00
  //   Éste circuito reconoce si la familia de operaciones es operaciones Aritméticas/Lógicas (ALU), Lectura/Escritura (DBI) o Condicional.
endmodule

module Fetch1 (
  output [1:0] OP_Y_SEL____0,
  output [3:0] out_2,
  output WR_AR,
  output EN_A,
  output [1:0] OP_ABI____W,
  output [2:0] out_6
);


  assign EN_A = 1'b1;
  assign OP_ABI____W = 2'b00;
  assign OP_Y_SEL____0 = 2'b00;
  assign out_2 = 4'b0101;
  assign out_6 = 3'b001;
  assign WR_AR = 1'b1;

  // Notes on the sheet:
  //   Fetch1:
  //   AR := PC
  //   goto Fetch2
  //   OP-ALU = @OR
  //   Next State = Fetch2
endmodule

module Fetch2 (
  input  WAIT,
  output [2:0] out_2,
  output SEL_D,
  output WR_IR,
  output EN_A,
  output RD,
  output [1:0] OP_ABI____W,
  output [2:0] Next_State
);

  Multiplexer #(.width(3)) multiplexer_1 (.in0(3'b010), .in1(3'b001), .out(Next_State), .sel(WAIT));  // open: en

  assign EN_A = 1'b1;
  assign OP_ABI____W = 2'b00;
  assign out_2 = 3'b000;
  assign RD = 1'b1;
  assign SEL_D = 1'b1;
  assign WR_IR = 1'b1;

  // Notes on the sheet:
  //   Fetch2:
  //   IR := Memw[AR]
  //   if WAIT goto fetch2
  //   else goto decode
  //   OP-DBI = @LDW
endmodule

module Decode (
  output [1:0] OP_Y_SEL____4,
  output [3:0] out_2,
  output WR_PC,
  output [2:0] Next_State
);


  assign Next_State = 3'b011;
  assign OP_Y_SEL____4 = 2'b01;
  assign out_2 = 4'b0000;
  assign WR_PC = 1'b1;

  // Notes on the sheet:
  //   decode:
  //   PC = PC + 4
  //   goto execute1
  //   OP-ALU = @ADD
endmodule

module exec1 (
  input  [4:0] in_1,
  input  in_2,
  output [3:0] OP_ALU,
  output [2:0] Next_State,
  output WR_AR,
  output [1:0] OP_Y_SEL,
  output WR_SR,
  output EN_A,
  output RD_DEST,
  output SEL_REG,
  output [1:0] OP_ABI,
  output WR_RD
);

  wire EN_A_DBI, RD_DEST_ALU, RD_DEST_Cond, SEL_REG_ALU, SEL_REG_DBI, WR_AR_DBI, WR_RD_ALU, WR_RD_Cond,
       WR_SR_ALU;
  wire [1:0] OP_ABI_DBI, OP_Y_SEL_ALU, OP_Y_SEL_Cond, OP_Y_SEL_DBI, Operation_Type;
  wire [2:0] Next_State_ALU, Next_State_Cond, Next_State_DBI;
  wire [3:0] OP_ALU_ALU, OP_ALU_Cond, OP_ALU_DBI;

  Multiplexer #(.select(2), .width(4)) multiplexer_1 (
    .in0(OP_ALU_Cond), .in1(OP_ALU_ALU), .in2(OP_ALU_DBI), .out(OP_ALU), .sel(Operation_Type));  // open: in3, en
  Multiplexer #(.select(2)) multiplexer_2 (
    .in0(RD_DEST_Cond), .in1(RD_DEST_ALU), .in2(1'b0), .out(RD_DEST), .sel(Operation_Type));  // open: in3, en
  Multiplexer #(.select(2)) multiplexer_3 (
    .in0(WR_RD_Cond), .in1(WR_RD_ALU), .in2(1'b0), .out(WR_RD), .sel(Operation_Type));  // open: in3, en
  Discriminate discriminate_1 (.in_1(in_1), .out_2(Operation_Type));
  Multiplexer #(.select(2), .width(2)) multiplexer_4 (
    .in0(OP_Y_SEL_Cond), .in1(OP_Y_SEL_ALU), .in2(OP_Y_SEL_DBI), .out(OP_Y_SEL), .sel(Operation_Type));  // open: in3, en
  Multiplexer #(.select(2), .width(3)) multiplexer_5 (
    .in0(Next_State_Cond), .in1(Next_State_ALU), .in2(Next_State_DBI), .out(Next_State), .sel(Operation_Type));  // open: in3, en
  Multiplexer #(.select(2)) multiplexer_6 (
    .in0(1'b0), .in1(WR_SR_ALU), .in2(1'b0), .out(WR_SR), .sel(Operation_Type));  // open: in3, en
  Multiplexer #(.select(2)) multiplexer_7 (
    .in0(1'b0), .in1(SEL_REG_ALU), .in2(SEL_REG_DBI), .out(SEL_REG), .sel(Operation_Type));  // open: in3, en
  Conditional_Instruction conditional_instruction_1 (
    .BR(in_2), .Next_State(Next_State_Cond), .in_2(in_1), .WR_RD(WR_RD_Cond), .RD_DEST(RD_DEST_Cond),
    .out_6(OP_Y_SEL_Cond), .out_7(OP_ALU_Cond));
  ALU_Instruction alu_instruction_1 (
    .in_1(in_1), .OP_ALU(OP_ALU_ALU), .SEL_REG(SEL_REG_ALU), .WR_RD(WR_RD_ALU), .WR_SR(WR_SR_ALU),
    .RD_DEST(RD_DEST_ALU), .OP_Y_SEL____INST(OP_Y_SEL_ALU), .Next_State(Next_State_ALU));
  DBI_Instruction dbi_instruction_1 (
    .SEL_REG(SEL_REG_DBI), .WR_AR(WR_AR_DBI), .EN_A(EN_A_DBI), .OP_ALU(OP_ALU_DBI), .OP_ABI(OP_ABI_DBI),
    .OP_Y_SEL(OP_Y_SEL_DBI), .Next_State(Next_State_DBI));
  Multiplexer #(.select(2)) multiplexer_8 (
    .in0(1'b0), .in1(1'b0), .in2(WR_AR_DBI), .out(WR_AR), .sel(Operation_Type));  // open: in3, en
  Multiplexer #(.select(2)) multiplexer_9 (
    .in0(1'b0), .in1(1'b0), .in2(EN_A_DBI), .out(EN_A), .sel(Operation_Type));  // open: in3, en
  Multiplexer #(.select(2), .width(2)) multiplexer_10 (
    .in0(2'b00), .in1(2'b00), .in2(OP_ABI_DBI), .out(OP_ABI), .sel(Operation_Type));  // open: in3, en

  // Other names for the same wires on the sheet: Instruction[4:0] = in_1

  // Notes on the sheet:
  //   Estado Exec1:
  //   según corresponda.
  //   Determina familia de operación con Discriminate y entrega resultados
  //   obtenidos de los circuitos ALU Instruction, DBI instruction o Conditional Instruction
endmodule

module ALU_Instruction (
  input  [4:0] in_1,
  output [3:0] OP_ALU,
  output SEL_REG,
  output WR_RD,
  output WR_SR,
  output RD_DEST,
  output [1:0] OP_Y_SEL____INST,
  output [2:0] Next_State
);


  assign Next_State = 3'b000;
  assign OP_ALU = in_1[4:1];
  assign OP_Y_SEL____INST = 2'b10;
  assign RD_DEST = 1'b1;
  assign SEL_REG = 1'b1;
  assign WR_RD = 1'b1;
  assign WR_SR = 1'b1;

  // Notes on the sheet:
  //   Instrucciones a entregar para la familia de operaciones aritméticas/lógicas en el estado exec1
endmodule

module DBI_Instruction (
  output SEL_REG,
  output WR_AR,
  output EN_A,
  output [3:0] OP_ALU,
  output [1:0] OP_ABI,
  output [1:0] OP_Y_SEL,
  output [2:0] Next_State
);


  assign EN_A = 1'b1;
  assign Next_State = 3'b100;
  assign OP_ABI = 2'b00;
  assign OP_ALU = 4'b0000;
  assign OP_Y_SEL = 2'b10;
  assign SEL_REG = 1'b1;
  assign WR_AR = 1'b1;

  // Notes on the sheet:
  //   Instrucciones a entregar para la familia de operaciones de Read/Write en el estado exec1
  //   OP-ALU = @ADD
  //   OP-ABI = @W
  //   OP-Y-SEL = @INST
  //   Next State = exec2
endmodule

module exec2 (
  input  [4:0] in_1,
  input  in_2,
  output [3:0] OP_ALU,
  output [2:0] Next_State,
  output EN_A,
  output RD,
  output [1:0] OP_Y_SEL,
  output WR,
  output [1:0] OP_ABI,
  output SEL_D,
  output RD_DEST,
  output SEL_REG,
  output EN_D,
  output [2:0] OP_DBI,
  output WR_PC,
  output WR_RD
);

  wire EN_A_DBI, EN_D_DBI, RD_DBI, RD_DEST_DBI, SEL_D_DBI, SEL_REG_Cond, SEL_REG_DBI, WR_DBI, WR_PC_Cond,
       WR_RD_DBI;
  wire [1:0] OP_ABI_DBI, OP_Y_SEL_Cond, OP_Y_SEL_DBI, Operation_Type;
  wire [2:0] Next_State_Cond, Next_State_DBI, OP_DBI_DBI;
  wire [3:0] OP_ALU_Cond, OP_ALU_DBI;

  Multiplexer #(.select(2), .width(4)) multiplexer_1 (
    .in0(OP_ALU_Cond), .in1(4'b0000), .in2(OP_ALU_DBI), .out(OP_ALU), .sel(Operation_Type));  // open: in3, en
  Multiplexer #(.select(2)) multiplexer_2 (
    .in0(1'b0), .in1(1'b0), .in2(RD_DEST_DBI), .out(RD_DEST), .sel(Operation_Type));  // open: in3, en
  Multiplexer #(.select(2), .width(3)) multiplexer_3 (
    .in0(3'b000), .in1(3'b000), .in2(OP_DBI_DBI), .out(OP_DBI), .sel(Operation_Type));  // open: in3, en
  Multiplexer #(.select(2), .width(2)) multiplexer_4 (
    .in0(OP_Y_SEL_Cond), .in1(2'b00), .in2(OP_Y_SEL_DBI), .out(OP_Y_SEL), .sel(Operation_Type));  // open: in3, en
  Discriminate discriminate_1 (.in_1(in_1), .out_2(Operation_Type));
  Multiplexer #(.select(2), .width(3)) multiplexer_5 (
    .in0(Next_State_Cond), .in1(3'b000), .in2(Next_State_DBI), .out(Next_State), .sel(Operation_Type));  // open: in3, en
  Multiplexer #(.select(2)) multiplexer_6 (
    .in0(1'b0), .in1(1'b0), .in2(WR_DBI), .out(WR), .sel(Operation_Type));  // open: in3, en
  Multiplexer #(.select(2)) multiplexer_7 (
    .in0(SEL_REG_Cond), .in1(1'b0), .in2(SEL_REG_DBI), .out(SEL_REG), .sel(Operation_Type));  // open: in3, en
  Multiplexer #(.select(2)) multiplexer_8 (
    .in0(WR_PC_Cond), .in1(1'b0), .in2(1'b0), .out(WR_PC), .sel(Operation_Type));  // open: in3, en
  Conditional_Instruction_2 conditional_instruction_2_1 (
    .WR_PC(WR_PC_Cond), .out_3(OP_Y_SEL_Cond), .out_4(OP_ALU_Cond), .Next_State(Next_State_Cond),
    .in_1(in_1), .SEL_REG(SEL_REG_Cond));
  DBI_Instruction_2 dbi_instruction_2_1 (
    .in_1(in_1), .WAIT(in_2), .SEL_REG(SEL_REG_DBI), .EN_D(EN_D_DBI), .RD_DEST(RD_DEST_DBI), .WR(WR_DBI),
    .EN_A(EN_A_DBI), .OP_DBI(OP_DBI_DBI), .out_9(OP_ALU_DBI), .OP_ABI(OP_ABI_DBI), .OP_Y_SEL(OP_Y_SEL_DBI),
    .Next_State(Next_State_DBI), .RD(RD_DBI), .SEL_D(SEL_D_DBI), .WR_RD(WR_RD_DBI));
  Multiplexer #(.select(2)) multiplexer_9 (
    .in0(1'b0), .in1(1'b0), .in2(EN_A_DBI), .out(EN_A), .sel(Operation_Type));  // open: in3, en
  Multiplexer #(.select(2), .width(2)) multiplexer_10 (
    .in0(2'b00), .in1(2'b00), .in2(OP_ABI_DBI), .out(OP_ABI), .sel(Operation_Type));  // open: in3, en
  Multiplexer #(.select(2)) multiplexer_11 (
    .in0(1'b0), .in1(1'b0), .in2(EN_D_DBI), .out(EN_D), .sel(Operation_Type));  // open: in3, en
  Multiplexer #(.select(2)) multiplexer_12 (
    .in0(1'b0), .in1(1'b0), .in2(WR_RD_DBI), .out(WR_RD), .sel(Operation_Type));  // open: in3, en
  Multiplexer #(.select(2)) multiplexer_13 (
    .in0(1'b0), .in1(1'b0), .in2(RD_DBI), .out(RD), .sel(Operation_Type));  // open: in3, en
  Multiplexer #(.select(2)) multiplexer_14 (
    .in0(1'b0), .in1(1'b0), .in2(SEL_D_DBI), .out(SEL_D), .sel(Operation_Type));  // open: in3, en

  // Other names for the same wires on the sheet: Instruction[4:0] = in_1; WAIT = in_2

  // Notes on the sheet:
  //   Estado exec2:
  //   Al igual que en exec1 se determina cual es la familia de operaciones a la que corresponde la operación
  //   en éste caso la familia de operaciones aritmético/lógicas no tiene elementos en éste estado.
endmodule

module DBI_Instruction_2 (
  input  [4:0] in_1,
  input  WAIT,
  output SEL_REG,
  output EN_D,
  output RD_DEST,
  output WR,
  output EN_A,
  output [2:0] OP_DBI,
  output [3:0] out_9,
  output [1:0] OP_ABI,
  output [1:0] OP_Y_SEL,
  output RD,
  output [2:0] Next_State,
  output SEL_D,
  output WR_RD
);

  wire comparator_1_eq, comparator_2_eq, comparator_3_eq, RD_or_WR;

  Multiplexer #(.width(3)) multiplexer_1 (.in0(3'b000), .in1(3'b100), .out(Next_State), .sel(WAIT));  // open: en
  Comparator #(.width(3), .mode("unsigned")) comparator_1 (
    .a(in_1[4:2]), .b(3'b111), .eq(comparator_1_eq));  // open: gt, lt
  Comparator #(.width(3), .mode("unsigned")) comparator_2 (
    .a(in_1[4:2]), .b(3'b110), .eq(comparator_2_eq));  // open: gt, lt
  or or_1 (RD_or_WR, comparator_1_eq, comparator_2_eq, comparator_3_eq);
  Comparator #(.width(3), .mode("unsigned")) comparator_3 (
    .a(in_1[4:2]), .b(3'b101), .eq(comparator_3_eq));  // open: gt, lt
  Multiplexer multiplexer_2 (.in0(1'b0), .in1(1'b1), .out(SEL_REG), .sel(RD_or_WR));  // open: en
  Multiplexer multiplexer_3 (.in0(1'b1), .in1(1'b0), .out(WR_RD), .sel(RD_or_WR));  // open: en
  Multiplexer multiplexer_4 (.in0(1'b0), .in1(1'b1), .out(EN_D), .sel(RD_or_WR));  // open: en
  Multiplexer multiplexer_5 (.in0(1'b0), .in1(1'b1), .out(WR), .sel(RD_or_WR));  // open: en
  Multiplexer #(.select(3), .width(2)) multiplexer_6 (
    .in0(2'b00), .in1(2'b01), .in2(2'b01), .in3(2'b10), .in4(2'b10), .in5(2'b00), .in6(2'b01), .in7(2'b10),
    .out(OP_ABI), .sel(in_1[4:2]));  // open: en
  Multiplexer multiplexer_7 (.in0(1'b1), .in1(1'b0), .out(RD), .sel(RD_or_WR));  // open: en
  Multiplexer multiplexer_8 (.in0(1'b1), .in1(1'b0), .out(SEL_D), .sel(RD_or_WR));  // open: en

  assign EN_A = 1'b1;
  assign OP_DBI = in_1[4:2];
  assign OP_Y_SEL = 2'b00;
  assign out_9 = 4'b0101;
  assign RD_DEST = 1'b1;

  // Notes on the sheet:
  //   OP-Y-SEL = @0
  //   if WAIT goto exec2
  //   else goto fetch1
  //   Instrucciones a entregar para la familia de operaciones de Read/Write para el estado exec2.
  //   OP-ALU = @OR
  //   Se distingue entre operaciones de Read y operaciones de Write, ya que se comportamiento difiere en algunas señales.
endmodule

module Circuito_combinacional (
  input  BR,
  input  [4:0] in_2,
  input  WAIT,
  input  [2:0] State,
  output [3:0] OP_ALU,
  output wr_ar,
  output sel_reg,
  output [1:0] OP_Y__SEL,
  output rd_dest,
  output en_a,
  output [1:0] OP_ABI,
  output sel_d,
  output wr_sr,
  output [2:0] OP_DBI,
  output wr_ir,
  output en_d,
  output rd,
  output wr,
  output wr_pc,
  output [2:0] State_2,
  output wr_Rd
);

  wire EN_A_Exec1, EN_A_Exec2, EN_A_Fetch1, EN_A_Fetch2, EN_D_Exec2, RD_DEST_Exec1, RD_DEST_Exec2, RD_Exec2,
       RD_Fetch2, SEL_D_Exec2, SEL_D_Fetch2, SEL_REG_Exec1, SEL_REG_Exec2, WR_AR_Exec1, WR_AR_Fetch1,
       WR_Exec2, WR_IR_Fetch2, WR_PC_Decode, WR_PC_Exec2, WR_RD_Exec1, WR_RD_Exec2, WR_SR_Exec1;
  wire [1:0] OP_ABI_Exec1, OP_ABI_Exec2, OP_ABI_Fetch1, OP_ABI_Fetch2, OP_Y_SEL_Decode, OP_Y_SEL_Exec1,
       OP_Y_SEL_Exec2, OP_Y_SEL_Fetch1;
  wire [2:0] Next_State_Decode, Next_State_Exec1, Next_State_Exec2, Next_State_Fetch1, Next_State_Fetch2,
       OP_DBI_Exec2, OP_DBI_Fetch2;
  wire [3:0] OP_ALU_Decode, OP_ALU_Exec1, OP_ALU_Exec2, OP_ALU_Fetch1;

  Fetch1 fetch1_1 (
    .OP_Y_SEL____0(OP_Y_SEL_Fetch1), .out_2(OP_ALU_Fetch1), .WR_AR(WR_AR_Fetch1), .EN_A(EN_A_Fetch1),
    .OP_ABI____W(OP_ABI_Fetch1), .out_6(Next_State_Fetch1));
  Fetch2 fetch2_1 (
    .WAIT(WAIT), .out_2(OP_DBI_Fetch2), .SEL_D(SEL_D_Fetch2), .WR_IR(WR_IR_Fetch2), .EN_A(EN_A_Fetch2),
    .RD(RD_Fetch2), .OP_ABI____W(OP_ABI_Fetch2), .Next_State(Next_State_Fetch2));
  Decode decode_1 (
    .OP_Y_SEL____4(OP_Y_SEL_Decode), .out_2(OP_ALU_Decode), .WR_PC(WR_PC_Decode),
    .Next_State(Next_State_Decode));
  exec2 exec2_1 (
    .in_1(in_2), .in_2(WAIT), .OP_ALU(OP_ALU_Exec2), .Next_State(Next_State_Exec2), .EN_A(EN_A_Exec2),
    .OP_Y_SEL(OP_Y_SEL_Exec2), .WR(WR_Exec2), .OP_ABI(OP_ABI_Exec2), .RD_DEST(RD_DEST_Exec2),
    .SEL_REG(SEL_REG_Exec2), .EN_D(EN_D_Exec2), .OP_DBI(OP_DBI_Exec2), .WR_PC(WR_PC_Exec2),
    .WR_RD(WR_RD_Exec2), .SEL_D(SEL_D_Exec2), .RD(RD_Exec2));
  exec1 exec1_1 (
    .in_1(in_2), .OP_ALU(OP_ALU_Exec1), .Next_State(Next_State_Exec1), .WR_AR(WR_AR_Exec1),
    .OP_Y_SEL(OP_Y_SEL_Exec1), .WR_SR(WR_SR_Exec1), .EN_A(EN_A_Exec1), .RD_DEST(RD_DEST_Exec1),
    .SEL_REG(SEL_REG_Exec1), .OP_ABI(OP_ABI_Exec1), .WR_RD(WR_RD_Exec1), .in_2(BR));
  Multiplexer #(.select(3), .width(4)) multiplexer_1 (
    .in0(OP_ALU_Fetch1), .in1(4'b0000), .in2(OP_ALU_Decode), .in3(OP_ALU_Exec1), .in4(OP_ALU_Exec2),
    .out(OP_ALU), .sel(State));  // open: in5, in6, in7, en
  Multiplexer #(.select(3), .width(2)) multiplexer_2 (
    .in0(OP_Y_SEL_Fetch1), .in1(2'b00), .in2(OP_Y_SEL_Decode), .in3(OP_Y_SEL_Exec1), .in4(OP_Y_SEL_Exec2),
    .out(OP_Y__SEL), .sel(State));  // open: in5, in6, in7, en
  Multiplexer #(.select(3), .width(2)) multiplexer_3 (
    .in0(OP_ABI_Fetch1), .in1(OP_ABI_Fetch2), .in2(2'b00), .in3(OP_ABI_Exec1), .in4(OP_ABI_Exec2),
    .out(OP_ABI), .sel(State));  // open: in5, in6, in7, en
  Multiplexer #(.select(3), .width(3)) multiplexer_4 (
    .in0(3'b000), .in1(OP_DBI_Fetch2), .in2(3'b000), .in3(3'b000), .in4(OP_DBI_Exec2), .out(OP_DBI),
    .sel(State));  // open: in5, in6, in7, en
  Multiplexer #(.select(3)) multiplexer_5 (
    .in0(WR_AR_Fetch1), .in1(1'b0), .in2(1'b0), .in3(WR_AR_Exec1), .in4(1'b0), .out(wr_ar), .sel(State));  // open: in5, in6, in7, en
  Multiplexer #(.select(3)) multiplexer_6 (
    .in0(EN_A_Fetch1), .in1(EN_A_Fetch2), .in2(1'b0), .in3(EN_A_Exec1), .in4(EN_A_Exec2), .out(en_a),
    .sel(State));  // open: in5, in6, in7, en
  Multiplexer #(.select(3)) multiplexer_7 (
    .in0(1'b0), .in1(SEL_D_Fetch2), .in2(1'b0), .in3(1'b0), .in4(SEL_D_Exec2), .out(sel_d), .sel(State));  // open: in5, in6, in7, en
  Multiplexer #(.select(3)) multiplexer_8 (
    .in0(1'b0), .in1(WR_IR_Fetch2), .in2(1'b0), .in3(1'b0), .in4(1'b0), .out(wr_ir), .sel(State));  // open: in5, in6, in7, en
  Multiplexer #(.select(3)) multiplexer_9 (
    .in0(1'b0), .in1(RD_Fetch2), .in2(1'b0), .in3(1'b0), .in4(RD_Exec2), .out(rd), .sel(State));  // open: in5, in6, in7, en
  Multiplexer #(.select(3)) multiplexer_10 (
    .in0(1'b0), .in1(1'b0), .in2(WR_PC_Decode), .in3(1'b0), .in4(WR_PC_Exec2), .out(wr_pc), .sel(State));  // open: in5, in6, in7, en
  Multiplexer #(.select(3)) multiplexer_11 (
    .in0(1'b0), .in1(1'b0), .in2(1'b0), .in3(WR_RD_Exec1), .in4(WR_RD_Exec2), .out(wr_Rd), .sel(State));  // open: in5, in6, in7, en
  Multiplexer #(.select(3)) multiplexer_12 (
    .in0(1'b0), .in1(1'b0), .in2(1'b0), .in3(SEL_REG_Exec1), .in4(SEL_REG_Exec2), .out(sel_reg), .sel(State));  // open: in5, in6, in7, en
  Multiplexer #(.select(3)) multiplexer_13 (
    .in0(1'b0), .in1(1'b0), .in2(1'b0), .in3(RD_DEST_Exec1), .in4(RD_DEST_Exec2), .out(rd_dest), .sel(State));  // open: in5, in6, in7, en
  Multiplexer #(.select(3)) multiplexer_14 (
    .in0(1'b0), .in1(1'b0), .in2(1'b0), .in3(WR_SR_Exec1), .out(wr_sr), .sel(State));  // open: in4, in5, in6, in7, en
  Multiplexer #(.select(3)) multiplexer_15 (
    .in0(1'b0), .in1(1'b0), .in2(1'b0), .in3(1'b0), .in4(EN_D_Exec2), .out(en_d), .sel(State));  // open: in5, in6, in7, en
  Multiplexer #(.select(3)) multiplexer_16 (
    .in0(1'b0), .in1(1'b0), .in2(1'b0), .in3(1'b0), .in4(WR_Exec2), .out(wr), .sel(State));  // open: in5, in6, in7, en
  Multiplexer #(.select(3), .width(3)) multiplexer_17 (
    .in0(Next_State_Fetch1), .in1(Next_State_Fetch2), .in2(Next_State_Decode), .in3(Next_State_Exec1),
    .in4(Next_State_Exec2), .out(State_2), .sel(State));  // open: in5, in6, in7, en

  // Other names for the same wires on the sheet: Current_State[2:0] = State; Instruction[4:0] = in_2

  // Notes on the sheet:
  //   Instruction
  //   Circuito combinacional del circuito secuencial que contiene los 5 circuitos que representan a los 5 estados en que puede encontrarse la unidad de control, en concordancia con el diagrama de estados.
endmodule

module Memoria_Estados (
  input  [2:0] in_1,
  input  CLK,
  output [2:0] out_3
);

  Register #(.width(3)) register_1 (.D(in_1), .Q(out_3), .clk(CLK));  // open: en, clr

  // Notes on the sheet:
  //   Previous State
  //   Memoria que guarda el estado en el que se encuentra el circuito producto de los resultados del ciclo anterior.
endmodule

module Conditional_Instruction_2 (
  input  [4:0] in_1,
  output WR_PC,
  output [1:0] out_3,
  output [3:0] out_4,
  output [2:0] Next_State,
  output SEL_REG
);

  Comparator #(.width(5), .mode("unsigned")) comparator_1 (.a(in_1), .b(5'b00001), .eq(SEL_REG));  // open: gt, lt
  Multiplexer #(.width(2)) multiplexer_1 (.in0(2'b11), .in1(2'b10), .out(out_3), .sel(SEL_REG));  // open: en

  assign Next_State = 3'b000;
  assign out_4 = 4'b0000;
  assign WR_PC = 1'b1;

  // Other names for the same wires on the sheet: JMPL = SEL_REG

  // Notes on the sheet:
  //   Instruction
  //   Instrucciones condicionales para el estado exec2.
  //   OP-Y-SEL = @DISP
  //   OP-Y-SEL=@INST
  //   OP-ALU = @ADD
endmodule

module Conditional_Instruction (
  input  BR,
  input  [4:0] in_2,
  output [2:0] Next_State,
  output WR_RD,
  output RD_DEST,
  output [1:0] out_6,
  output [3:0] out_7
);

  wire JMPL;
  wire [2:0] multiplexer_1_out;

  Multiplexer #(.width(3)) multiplexer_1 (.in0(3'b000), .in1(3'b100), .out(multiplexer_1_out), .sel(BR));  // open: en
  Comparator #(.width(5), .mode("unsigned")) comparator_1 (.a(in_2), .b(5'b00001), .eq(JMPL));  // open: gt, lt
  Multiplexer #(.width(3)) multiplexer_2 (
    .in0(multiplexer_1_out), .in1(3'b100), .out(Next_State), .sel(JMPL));  // open: en
  Multiplexer multiplexer_3 (.in0(1'b0), .in1(1'b1), .out(WR_RD), .sel(JMPL));  // open: en
  Multiplexer multiplexer_4 (.in0(1'b0), .in1(1'b1), .out(RD_DEST), .sel(JMPL));  // open: en
  Multiplexer #(.width(2)) multiplexer_5 (.in0(2'b00), .in1(2'b01), .out(out_6), .sel(JMPL));  // open: en

  assign out_7 = 4'b0000;

  // Notes on the sheet:
  //   Instruction
  //   Se chequea si la instrucción corresponde a JMPL (00001), ya que su comportamiento
  //   es distinto al del resto de la familia de operaciones condicionales
  //   Instrucciones a entregar para la familia de operaciones condicionales en el estado exec1
  //   OP-Y-SEL = @4 (01)
  //   OP-ALU = @ADD
endmodule
